# Fritzing sketch WaterSystem (saved by Fritzing 1.0.4)

parts:
  Part1 = Arduino Uno (Rev3)
  Part2 = Soil Moisture Sensor
  IC1 = DIP - 6 pins [chip_label="5V RELAY" package="DIP (Dual Inline) [THT]"]
  VCC1 = Battery [internal_resistance=0.1Ω]
  WATER_PUMP1 = water pump/motor  # not connected

nets:
  N1: Part1.A0, Part2.SIG
  N2: Part1.D3_PWM, IC1.IN
  3V3: Part1.3V3, Part2.VCC
  N3: Part1.5V, IC1.DC+
  GND: Part1.GND, Part2.GND, IC1.DC-
  N4: IC1.CO, VCC1.+

custom parts:
  DIP - 6 pins: A DIP stand-in part for whatever IC you want. With 6 pins on a 300mil dual inline package (DIP) footprint.
  water pump/motor: WATER PUMP BY ARDUBLOCKTR
